# Fritzing sketch project_with_RFID-522 (saved by Fritzing 0.9.0b)

parts:
  Componente1 = Arduino Uno (Rev3)
  Componente2 = RFID-RC522-v3
  Relay_5V1 = Keyes Relay [package=THT]
  LED1 = RGB LED (com. cathode, rgb) [package="5 mm [THT]"]
  R1 = Resistor [tolerance=±5% resistance=680 package=THT]
  R2 = Resistor [tolerance=±5% resistance=680 package=THT]
  R3 = Resistor [tolerance=±5% resistance=680 package=THT]

nets:
  N1: Componente1.D9_PWM, Componente2.RST
  N2: Componente1.D10_PWM/SS, Componente2.SDA
  N3: Componente1.D11_PWM/MOSI, Componente2.MOSI
  N4: Componente1.D12/MISO, Componente2.MISO
  N5: Componente1.D13/SCK, Componente2.SCK
  GND: Componente1.GND, Componente2.IRQ, Componente2.GND, Relay_5V1.ground, LED1.common_cathode
  N6: Componente1.D3_PWM, R2.Pin_1
  N7: Componente1.D5_PWM, R3.Pin_1
  N8: Componente1.D6_PWM, R1.Pin_1
  N9: Componente1.D7, Relay_5V1.signal
  3V3: Componente1.3V3, Componente2.3.3V
  N10: Componente1.5V, Relay_5V1.power
  N11: Relay_5V1.C, Relay_5V1.NO
  N12: LED1.red_anode, R1.Pin_0
  N13: LED1.green_anode, R3.Pin_0
  N14: LED1.blue_anode, R2.Pin_0

notes:
  3,3 V
  RST
  GND
  SDA
  SCK
  MOSI
  MISO
  5 V
  SIGNAL

custom parts:
  RFID-RC522-v3: A simple China made RFID-RC522 Reader (6x4 cm); do check the pin labels, as this is a MFRC522 based clone.
  Keyes Relay: The Keyes 5V relay module is suitable for SCM development, home appliance control. It uses a 5V~12V TIL control signal which can control DC / AC signal.
