# Fritzing sketch MT8870_with_Arduino (saved by Fritzing 0.9.0b)
breadboards: 2

parts:
  IC1 = IC, DIP package, 18 pins [chip_label=MT8870]
  C1 = Ceramic Capacitor [capacitance=100nF voltage=16V package="100 mil [THT, multilayer]"]
  R1 = Trimmer Potentiometer [maximum_resistance=100kΩ package=THT]
  R2 = Trimmer Potentiometer [maximum_resistance=100kΩ package=THT]
  J1 = Screw terminal - 2 pins [package=THT]
  XTAL1 = Crystal [frequency="16 Mhz" part_number=" 3.579545 MHz" package=THT]
  R7 = Resistor [tolerance=±5% resistance=680 package=THT]
  R5 = Resistor [tolerance=±5% resistance=680 package=THT]
  R3 = Resistor [tolerance=±5% resistance=680 package=THT]
  R4 = Resistor [tolerance=±5% resistance=680 package=THT]
  R6 = Resistor [tolerance=±5% resistance=680 package=THT]
  LED1 = LED - 5mm [color="Green (555nm)" package="5 mm [THT]"]
  LED2 = LED - 5mm [color="Red (633nm)" package="5 mm [THT]"]
  LED3 = LED - 5mm [color="Red (633nm)" package="5 mm [THT]"]
  LED4 = LED - 5mm [color="Red (633nm)" package="5 mm [THT]"]
  LED5 = LED - 5mm [color="Red (633nm)" package="5 mm [THT]"]
  C2 = Ceramic Capacitor [capacitance=100nF voltage=16V package="100 mil [THT, multilayer]"]
  R8 = Resistor [tolerance=±5% resistance=390k package=THT]
  Componente1 = Arduino Nano (Rev3.0)

nets:
  N1: IC1.pin1, IC1.pin4
  N2: IC1.pin2, R1.wiper, R2.leg1
  N3: IC1.pin3, R2.wiper
  N4: IC1.pin7, XTAL1.pin_1
  N5: IC1.pin8, XTAL1.pin_0
  GND: IC1.pin9, J1.pin1, LED1.cathode, LED2.cathode, LED3.cathode, LED4.cathode, LED5.cathode, Componente1.GND
  5V: IC1.pin10, IC1.pin18, C2.0, Componente1.5V
  N6: IC1.pin11, R7.Pin_0, Componente1.D6
  N7: IC1.pin12, R6.Pin_0, Componente1.D5
  N8: IC1.pin13, R5.Pin_0, Componente1.D4
  N9: IC1.pin14, R4.Pin_0, Componente1.D3
  N10: IC1.pin15, R3.Pin_0, Componente1.D2
  N11: IC1.pin16, R8.Pin_1
  N12: IC1.pin17, C2.1, R8.Pin_0
  N13: C1.0, J1.pin2
  N14: C1.1, R1.leg2
  N15: R7.Pin_1, LED5.anode
  N16: R5.Pin_1, LED3.anode
  N17: R3.Pin_1, LED1.anode
  N18: R4.Pin_1, LED2.anode
  N19: R6.Pin_1, LED4.anode

notes:
  R1 = 102KΩ ± 1%
  R2 = 71.5KΩ ± 1%
  R3 = 390KΩ ±1 %
  C1,C2 = 100 nF ± 5%
  X1 = 3.579545 MHz ± 0.1%
  VDD = 5.0V ± 5%
